# Fritzing sketch encoderElectronic (saved by Fritzing 0.9.3b)
breadboards: 1

parts:
  Q1 = LTR-301 [package=ltr-301]
  Composant1 = Arduino Mega 2560 (Rev3)
  D1 = LTE-302 [package=lte-302]
  BC547 = NPN-Transistor [package="TO92 [THT]"]
  2N222A = TRANSISTOR_NPN - 2N2222 [package=to-92]
  U1 = Voltage Regulator - 5V [package="DPak [SMD]"]
  R8 = Resistor [tolerance=±5% resistance=10k package=THT]
  R10 = Resistor [tolerance=±5% resistance=150 package=THT]
  R11 = Resistor [tolerance=±5% resistance=1M package=THT]

nets:
  N1: Q1.C, R11.Pin_0
  N2: Q1.E, D1.C, BC547.B, R8.Pin_1
  GND: Composant1.A8, Composant1.GND, BC547.E, 2N222A.E, U1.GND, R10.Pin_1, R11.Pin_1
  N3: Composant1.D48, 2N222A.B
  N4: D1.A, R10.Pin_0
  N5: BC547.C, R8.Pin_0
  N6: 2N222A.C, U1.output_voltage

notes:
  IR emitter
  IR receiver
  wheel encoder
  power
  150
  1Mg
  10K

custom parts:
  TRANSISTOR_NPN - 2N2222: Generic NPN BJT. MMBT2222 is the common NPN we use. Double check against datasheet- not all devices are the same!
