# Fritzing sketch encoderV2 (saved by Fritzing 0.9.1b)
breadboards: 1

parts:
  Q1 = LTR-301 [package=ltr-301]
  D1 = LTE-302 [package=lte-302]
  2N1 = TRANSISTOR_NPN - 2N2222 [package=to-92]
  Composant1 = Arduino Mega 2560 (Rev3)
  R6 = Resistor150 [package="0402 [SMD]"]
  R3 = Resistor [package="0402 [SMD]"]
  R1 = Resistor 10K [package="0402 [SMD]"]

nets:
  N1: Q1.C, 2N1.B, R1.Pin_1
  N2: Q1.E, D1.C, R3.Pin_0
  N3: D1.A, R6.Pin_0
  N4: 2N1.E, R6.Pin_1, R1.Pin_0
  N5: 2N1.C, Composant1.A8, R3.Pin_1

notes:
  IR emitter
  IR receiver
  wheel encoder

custom parts:
  TRANSISTOR_NPN - 2N2222: Generic NPN BJT. MMBT2222 is the common NPN we use. Double check against datasheet- not all devices are the same!
  Resistor150: Resistor Basic schematic elements and footprints for 0603, 1206, and PTH resistors.
  Resistor: Resistor Basic schematic elements and footprints for 0603, 1206, and PTH resistors.
  Resistor 10K: Resistor Basic schematic elements and footprints for 0603, 1206, and PTH resistors.
